# Fritzing sketch SubCtl_2Sonic (saved by Fritzing 0.9.0b)
perfboards: 1

parts:
  Bauteil1 = Arduino Pro Mini v13
  R1 = Resistor [tolerance=±5% resistance=220 package=THT]
  R2 = Resistor [tolerance=±5% resistance=220 package=THT]
  LED1 = LED - 3mm [color="Red (633nm)" package="3 mm [THT]"]
  LED2 = LED - 3mm [color="Red (633nm)" package="3 mm [THT]"]
  LED3 = LED - 3mm [color="Yellow (595nm)" package="3 mm [THT]"]
  LED4 = LED - 3mm [color="Yellow (595nm)" package="3 mm [THT]"]
  LED5 = LED - 3mm [color="Green (565nm)" package="3 mm [THT]"]
  LED6 = LED - 3mm [color="Green (565nm)" package="3 mm [THT]"]
  LED7 = LED - 3mm [color="Blue (525nm)" package="3 mm [THT]"]
  LED8 = LED - 3mm [color="Blue (525nm)" package="3 mm [THT]"]
  R3 = Resistor [tolerance=±5% resistance=150 package=THT]
  R4 = Resistor [tolerance=±5% resistance=150 package=THT]
  R5 = Resistor [tolerance=±5% resistance=150 package=THT]
  R6 = Resistor [tolerance=±5% resistance=150 package=THT]
  R7 = Resistor [tolerance=±5% resistance=100 package=THT]
  R8 = Resistor [tolerance=±5% resistance=100 package=THT]

nets:
  N1: Bauteil1.VCC, Bauteil1.A3
  N2: Bauteil1.GND, Bauteil1.RESET
  N3: Bauteil1.A1, R2.Pin_0
  N4: Bauteil1.A0, R5.Pin_0
  N5: Bauteil1.D13/SCK, R3.Pin_0
  N6: Bauteil1.D12/MISO, R8.Pin_0
  N7: Bauteil1.D7, R7.Pin_0
  N8: Bauteil1.D6_PWM, R6.Pin_0
  N9: Bauteil1.D5_PWM, R4.Pin_0
  N10: Bauteil1.D4, R1.Pin_0
  N11: R1.Pin_1, LED1.cathode
  N12: R2.Pin_1, LED2.cathode
  N13: LED3.cathode, R4.Pin_1
  N14: LED4.cathode, R5.Pin_1
  N15: LED5.cathode, R6.Pin_1
  N16: LED6.cathode, R3.Pin_1
  N17: LED7.cathode, R8.Pin_1
  N18: LED8.cathode, R7.Pin_1

notes:
  Zum Pegelwandler / I2C
  Zum Pegelwandler / GPIO RPi
  zum HC SR04 vorne
  zum HC SR04 hinten
  Zur Spannungsversorgung
